// Logisim project 8085multiprocessor.circ as structural Verilog: 1 circuit, main circuit main
module main (
);

  wire PC_p1, PC_p2, SP_p1, SP_p2;

  Register #(.width(8)) Accumulator ();  // open: D, en, Q, clk, clr
  Register #(.width(8)) B ();  // open: D, en, Q, clk, clr
  Register #(.width(8)) C ();  // open: D, en, Q, clk, clr
  Register #(.width(8)) D ();  // open: D, en, Q, clk, clr
  Register #(.width(8)) E ();  // open: D, en, Q, clk, clr
  Register #(.width(8)) H ();  // open: D, en, Q, clk, clr
  Register #(.width(8)) L ();  // open: D, en, Q, clk, clr
  // Register #(.width(16)) PC: pin names not known; wires that end beside it: PC_p1, PC_p2
  // Register #(.width(16)) SP: pin names not known; wires that end beside it: SP_p1, SP_p2
  Register #(.width(8)) Flags ();  // open: D, en, Q, clk, clr
endmodule
